# Fritzing sketch MCP4251_tcon (saved by Fritzing 0.8.7b)
circuit board: 6.88566cm x 5.36311cm
breadboards: 1

parts:
  R1 = Resistor [tolerance=±5% resistance=220 package=THT]
  LED1 = LED - 5mm [color="Green (555nm)" package="5 mm [THT]"]
  R2 = Resistor [tolerance=±5% resistance=220 package=THT]
  LED2 = LED - 5mm [color="Green (555nm)" package="5 mm [THT]"]
  R3 = Resistor [tolerance=±5% resistance=4.7k package=THT]
  Part1 = Arduino Uno (Rev3) - ICSP
  U3 = MCP4251 [package="DIP14 [THT]"]

nets:
  N1: R1.Pin_0, U3.P0W
  N2: R1.Pin_1, LED1.anode
  GND: LED1.cathode, LED2.cathode, R3.Pin_0, Part1.GND, U3.VSS, U3.P1B, U3.P0B
  N3: R2.Pin_0, U3.P1W
  N4: R2.Pin_1, LED2.anode
  N5: R3.Pin_1, Part1.D7, U3.SHDN
  5V: Part1.5V, U3.P1A, U3.P0A, U3.WP, U3.VDD
  N6: Part1.D10_PWM/SS, U3.CS
  N7: Part1.D11_PWM/MOSI, U3.SDI
  N8: Part1.D12/MISO, U3.SDO
  N9: Part1.D13/SCK, U3.SCK

notes:
  Matthew McMillan
  @matthewmcmillan
  http://matthewcmcmillan.blogspot.com/
  Using a MCP4251 Digital Pot with an Arduino Uno

custom parts:
  MCP4251: Dual SPI Digital Potentiometer

// code stored in the sketch: Blink.ino
/*
  Blink
  Turns on an LED on for one second, then off for one second, repeatedly.
 
  This example code is in the public domain.
 */

void setup() {                
  // initialize the digital pin as an output.
  // Pin 13 has an LED connected on most Arduino boards:
  pinMode(13, OUTPUT);     
}

void loop() {
  digitalWrite(13, HIGH);   // set the LED on
  delay(1000);              // wait for a second
  digitalWrite(13, LOW);    // set the LED off
  delay(1000);              // wait for a second
}
