# Fritzing sketch Speedometer_7seg (saved by Fritzing 0.8.3b)
breadboards: 1

parts:
  7SEG1 = 7-Segment LED I2C Backpack (green)
  Part2 = Arduino Uno (Rev3)
  R1 = PHOTOCELL [package=photocell-kit]
  R2 = Resistor [tolerance=±5% resistance=1k package="1206 [SMD]"]

nets:
  N1: 7SEG1.V+, Part2.5V, R1.P$2
  GND: 7SEG1.GND, Part2.GND, R2.Pin_0
  N2: 7SEG1.SDA, Part2.A4/SDA
  N3: 7SEG1.SCL, Part2.A5/SCL
  N4: Part2.A0, R1.P$1, R2.Pin_1

notes:
  To VSS

custom parts:
  7-Segment LED I2C Backpack (green): 4-digit, 7-segment LED Display with I2C Control
